// Logisim project Practica02.circ as structural Verilog: 9 circuits, main circuit sum
module Ejercicio5 (
  input  A7,
  input  A6,
  input  A5,
  input  A4,
  input  A3,
  input  A2,
  input  A1,
  input  A0,
  input  [2:0] _001_OR,
  input  _1_Resta,
  input  B7,
  input  B6,
  input  B5,
  input  B4,
  input  B3,
  input  B2,
  input  B1,
  input  B0,
  output out_19,
  output out_20,
  output out_21,
  output out_22,
  output out_23,
  output out_24,
  output out_25,
  output out_26,
  output Overflow
);

  Alu_prueba alu_prueba_1 (
    .in_1(A7), .in_2(A6), .in_3(A5), .in_4(A4), .in_5(A3), .in_6(A2), .in_7(A1), .in_8(A0), .in_9(_001_OR),
    .in_11(B7), .in_12(B6), .in_13(B5), .in_14(B4), .in_15(B3), .in_16(B2), .in_17(B1), .in_18(B0),
    .out_27(Overflow), .out_19(out_19), .out_20(out_20), .out_21(out_21), .out_22(out_22), .out_23(out_23),
    .out_24(out_24), .out_25(out_25), .out_26(out_26), .in_10(_1_Resta));

  // Notes on the sheet:
  //   _001_OR: pull=up
  //   Entrada A
  //   Entrada B
  //   000 AND
  //   010 ADICIÓN
  //   011 SUSTRACCIÓN
  //   100 IGUALDAD
  //   101 NOR
  //   Salida 8 Bits
  //   0 Otro Caso
endmodule

// Suma
module sum (
  input  in_1,
  input  in_2,
  input  in_3,
  output out_4,
  output out_5
);

  wire and_1_out, and_2_out, and_3_out, and_4_out, not_1_out, not_2_out, not_3_out;

  out out_1 (.in_1(in_1), .in_2(in_2), .in_3(in_3), .out_4(out_4));
  not not_1 (not_1_out, in_1);
  not not_2 (not_2_out, in_2);
  not not_3 (not_3_out, in_3);
  and and_1 (and_1_out, not_1_out, not_2_out, in_3);
  and and_2 (and_2_out, not_1_out, in_2, not_3_out);
  or or_1 (out_5, and_1_out, and_2_out, and_3_out, and_4_out);
  and and_3 (and_3_out, in_1, not_2_out, not_3_out);
  and and_4 (and_4_out, in_1, in_2, in_3);
endmodule

module out (
  input  in_1,
  input  in_2,
  input  in_3,
  output out_4
);

  wire and_1_out, and_2_out, and_3_out;

  and and_1 (and_1_out, in_2, in_3);
  and and_2 (and_2_out, in_1, in_3);
  and and_3 (and_3_out, in_1, in_2);
  or or_1 (out_4, and_1_out, and_2_out, and_3_out);
endmodule

module ALU_Mod (
  input  [2:0] in_1,
  input  A,
  input  B,
  input  in_4,
  output S,
  output Carry_Out
);

  wire and_2_out, AND_out, not_1_out, not_2_out, not_3_out, or_2_out, OR_out, sum_1_out_5;

  sum sum_1 (.in_1(in_4), .in_2(B), .in_3(A), .out_4(Carry_Out), .out_5(sum_1_out_5));
  not not_1 (not_1_out, sum_1_out_5);
  not not_2 (not_2_out, in_4);
  and OR (OR_out, A, B);
  or AND (AND_out, A, B);
  not not_3 (not_3_out, AND_out);
  and and_2 (and_2_out, not_1_out, not_2_out);
  or or_2 (or_2_out, OR_out, and_2_out);
  Multiplexer #(.select(3), .enable("false")) multiplexer_1 (
    .in0(OR_out), .in1(AND_out), .in2(sum_1_out_5), .in3(sum_1_out_5), .in4(or_2_out), .in5(not_3_out),
    .out(S), .sel(in_1));  // open: in6, in7

  // Notes on the sheet:
  //   in_4: pull=up
  //   01 OR
  //   00 AND
  //   10 ADICIÓN
endmodule

module Ejercicio1 (
  input  [1:0] _00_AND,
  input  A,
  input  B,
  output S
);

  wire AND_out, OR_out;

  and OR (OR_out, A, B);
  or AND (AND_out, A, B);
  Multiplexer #(.select(2), .enable("false")) multiplexer_1 (
    .in0(OR_out), .in1(AND_out), .out(S), .sel(_00_AND));  // open: in2, in3

  // Notes on the sheet:
  //   01 OR
endmodule

module Alu_prueba (
  input  in_1,
  input  in_2,
  input  in_3,
  input  in_4,
  input  in_5,
  input  in_6,
  input  in_7,
  input  in_8,
  input  [2:0] in_9,
  input  in_10,
  input  in_11,
  input  in_12,
  input  in_13,
  input  in_14,
  input  in_15,
  input  in_16,
  input  in_17,
  input  in_18,
  output out_19,
  output out_20,
  output out_21,
  output out_22,
  output out_23,
  output out_24,
  output out_25,
  output out_26,
  output out_27
);

  wire alu_mod_1_carry_out, alu_mod_1_s, alu_mod_2_carry_out, alu_mod_3_carry_out, alu_mod_4_carry_out,
       alu_mod_5_carry_out, alu_mod_6_carry_out, alu_mod_7_carry_out, multiplexer_1_out, multiplexer_2_out,
       multiplexer_3_out, multiplexer_4_out, multiplexer_5_out, multiplexer_6_out, multiplexer_7_out,
       multiplexer_8_out, not_1_out, not_2_out, not_3_out, not_4_out, not_5_out, not_6_out, not_7_out,
       not_8_out;

  Multiplexer #(.enable("false")) multiplexer_1 (.in0(in_12), .in1(not_2_out), .out(multiplexer_1_out), .sel(in_10));
  Multiplexer #(.enable("false")) multiplexer_2 (.in0(in_11), .in1(not_1_out), .out(multiplexer_2_out), .sel(in_10));
  not not_1 (not_1_out, in_11);
  not not_2 (not_2_out, in_12);
  Multiplexer #(.enable("false")) multiplexer_3 (.in0(in_13), .in1(not_3_out), .out(multiplexer_3_out), .sel(in_10));
  not not_3 (not_3_out, in_13);
  Multiplexer #(.enable("false")) multiplexer_4 (.in0(in_15), .in1(not_4_out), .out(multiplexer_4_out), .sel(in_10));
  Multiplexer #(.enable("false")) multiplexer_5 (.in0(in_14), .in1(not_5_out), .out(multiplexer_5_out), .sel(in_10));
  not not_4 (not_4_out, in_15);
  not not_5 (not_5_out, in_14);
  ALU_Mod alu_mod_1 (
    .A(in_8), .B(multiplexer_7_out), .in_4(in_10), .in_1(in_9), .S(alu_mod_1_s),
    .Carry_Out(alu_mod_1_carry_out));
  Multiplexer #(.enable("false")) multiplexer_6 (.in0(in_16), .in1(not_6_out), .out(multiplexer_6_out), .sel(in_10));
  not not_6 (not_6_out, in_16);
  ALU_Mod alu_mod_2 (
    .A(in_7), .B(multiplexer_8_out), .in_4(alu_mod_1_carry_out), .in_1(in_9), .S(out_25),
    .Carry_Out(alu_mod_2_carry_out));
  Multiplexer #(.enable("false")) multiplexer_7 (.in0(in_18), .in1(not_7_out), .out(multiplexer_7_out), .sel(in_10));
  Multiplexer #(.enable("false")) multiplexer_8 (.in0(in_17), .in1(not_8_out), .out(multiplexer_8_out), .sel(in_10));
  not not_7 (not_7_out, in_18);
  not not_8 (not_8_out, in_17);
  ALU_Mod alu_mod_3 (
    .A(in_6), .B(multiplexer_6_out), .in_4(alu_mod_2_carry_out), .in_1(in_9), .S(out_24),
    .Carry_Out(alu_mod_3_carry_out));
  ALU_Mod alu_mod_4 (
    .A(in_5), .B(multiplexer_4_out), .in_4(alu_mod_3_carry_out), .in_1(in_9), .S(out_23),
    .Carry_Out(alu_mod_4_carry_out));
  ALU_Mod alu_mod_5 (
    .A(in_4), .B(multiplexer_5_out), .in_4(alu_mod_4_carry_out), .in_1(in_9), .S(out_22),
    .Carry_Out(alu_mod_5_carry_out));
  ALU_Mod alu_mod_6 (
    .A(in_3), .B(multiplexer_3_out), .in_4(alu_mod_5_carry_out), .in_1(in_9), .S(out_21),
    .Carry_Out(alu_mod_6_carry_out));
  ALU_Mod alu_mod_7 (
    .A(in_2), .B(multiplexer_1_out), .in_4(alu_mod_6_carry_out), .in_1(in_9), .S(out_20),
    .Carry_Out(alu_mod_7_carry_out));
  ALU_Mod alu_mod_8 (
    .A(in_1), .B(multiplexer_2_out), .in_4(alu_mod_7_carry_out), .in_1(in_9), .S(out_19), .Carry_Out(out_27));
  Multiplexer #(.select(3), .enable("false")) multiplexer_9 (
    .in0(alu_mod_1_s), .in1(alu_mod_1_s), .in2(alu_mod_1_s), .in3(alu_mod_1_s), .in4(alu_mod_1_s),
    .in5(alu_mod_1_s), .out(out_26), .sel(in_9));  // open: in6, in7
endmodule

module Ejercicio2 (
  input  [2:0] _01_OR,
  input  A,
  input  B,
  input  Carry_In,
  output S,
  output Carry_Out
);

  wire AND_out, OR_out, sum_1_out_5;

  and OR (OR_out, A, B);
  or AND (AND_out, A, B);
  sum sum_1 (.in_1(Carry_In), .in_2(B), .in_3(A), .out_4(Carry_Out), .out_5(sum_1_out_5));
  Multiplexer #(.select(3), .enable("false")) multiplexer_1 (
    .in0(OR_out), .in1(AND_out), .in2(sum_1_out_5), .out(S), .sel(_01_OR));  // open: in3, in4, in5, in6, in7

  // Notes on the sheet:
  //   00 AND
  //   10 ADICIÓN
endmodule

module Ejercicio4 (
  input  A0,
  input  A1,
  input  A2,
  input  A3,
  input  A4,
  input  A5,
  input  A6,
  input  A7,
  input  [2:0] Seleccionador,
  input  Carry_in,
  input  B0,
  input  B1,
  input  B2,
  input  B3,
  input  B4,
  input  B5,
  input  B6,
  input  B7,
  output out_19,
  output out_20,
  output out_21,
  output out_22,
  output Resultados,
  output out_24,
  output out_25,
  output out_26,
  output Carry_out
);

  wire ejercicio3_1_carry_out, ejercicio3_1_s, ejercicio3_2_carry_out, ejercicio3_3_carry_out,
       ejercicio3_4_carry_out, ejercicio3_5_carry_out, ejercicio3_6_carry_out, ejercicio3_7_carry_out,
       multiplexer_1_out, multiplexer_2_out, multiplexer_3_out, multiplexer_4_out, multiplexer_5_out,
       multiplexer_6_out, multiplexer_7_out, multiplexer_8_out, not_1_out, not_2_out, not_3_out, not_4_out,
       not_5_out, not_6_out, not_7_out, not_8_out;

  Multiplexer #(.enable("false")) multiplexer_1 (.in0(B1), .in1(not_1_out), .out(multiplexer_1_out), .sel(Carry_in));
  Multiplexer #(.enable("false")) multiplexer_2 (.in0(B0), .in1(not_2_out), .out(multiplexer_2_out), .sel(Carry_in));
  not not_1 (not_1_out, B1);
  not not_2 (not_2_out, B0);
  Multiplexer #(.enable("false")) multiplexer_3 (.in0(B2), .in1(not_3_out), .out(multiplexer_3_out), .sel(Carry_in));
  not not_3 (not_3_out, B2);
  Multiplexer #(.enable("false")) multiplexer_4 (.in0(B3), .in1(not_4_out), .out(multiplexer_4_out), .sel(Carry_in));
  Multiplexer #(.enable("false")) multiplexer_5 (.in0(B4), .in1(not_5_out), .out(multiplexer_5_out), .sel(Carry_in));
  not not_4 (not_4_out, B3);
  not not_5 (not_5_out, B4);
  Ejercicio3 ejercicio3_1 (
    .A(A7), .B(multiplexer_8_out), .in_4(Carry_in), .in_1(Seleccionador), .S(ejercicio3_1_s),
    .Carry_Out(ejercicio3_1_carry_out));
  Multiplexer #(.enable("false")) multiplexer_6 (.in0(B5), .in1(not_6_out), .out(multiplexer_6_out), .sel(Carry_in));
  not not_6 (not_6_out, B5);
  Ejercicio3 ejercicio3_2 (
    .A(A6), .B(multiplexer_7_out), .in_4(ejercicio3_1_carry_out), .in_1(Seleccionador), .S(out_25),
    .Carry_Out(ejercicio3_2_carry_out));
  Multiplexer #(.enable("false")) multiplexer_7 (.in0(B6), .in1(not_8_out), .out(multiplexer_7_out), .sel(Carry_in));
  Multiplexer #(.enable("false")) multiplexer_8 (.in0(B7), .in1(not_7_out), .out(multiplexer_8_out), .sel(Carry_in));
  not not_7 (not_7_out, B7);
  not not_8 (not_8_out, B6);
  Ejercicio3 ejercicio3_3 (
    .A(A5), .B(multiplexer_6_out), .in_4(ejercicio3_2_carry_out), .in_1(Seleccionador), .S(out_24),
    .Carry_Out(ejercicio3_3_carry_out));
  Ejercicio3 ejercicio3_4 (
    .A(A4), .B(multiplexer_5_out), .in_4(ejercicio3_3_carry_out), .in_1(Seleccionador), .S(Resultados),
    .Carry_Out(ejercicio3_4_carry_out));
  Ejercicio3 ejercicio3_5 (
    .A(A3), .B(multiplexer_4_out), .in_4(ejercicio3_4_carry_out), .in_1(Seleccionador), .S(out_22),
    .Carry_Out(ejercicio3_5_carry_out));
  Ejercicio3 ejercicio3_6 (
    .A(A2), .B(multiplexer_3_out), .in_4(ejercicio3_5_carry_out), .in_1(Seleccionador), .S(out_21),
    .Carry_Out(ejercicio3_6_carry_out));
  Ejercicio3 ejercicio3_7 (
    .A(A1), .B(multiplexer_1_out), .in_4(ejercicio3_6_carry_out), .in_1(Seleccionador), .S(out_20),
    .Carry_Out(ejercicio3_7_carry_out));
  Ejercicio3 ejercicio3_8 (
    .A(A0), .B(multiplexer_2_out), .in_4(ejercicio3_7_carry_out), .in_1(Seleccionador), .S(out_19),
    .Carry_Out(Carry_out));
  Multiplexer #(.select(3), .enable("false")) multiplexer_9 (
    .in0(ejercicio3_1_s), .in1(ejercicio3_1_s), .in2(ejercicio3_1_s), .in3(ejercicio3_1_s), .out(out_26),
    .sel(Seleccionador));  // open: in4, in5, in6, in7
endmodule

module Ejercicio3 (
  input  [2:0] in_1,
  input  A,
  input  B,
  input  in_4,
  output S,
  output Carry_Out
);

  wire and_2_out, AND_out, not_1_out, not_2_out, or_2_out, OR_out, sum_1_out_5;

  and OR (OR_out, A, B);
  or AND (AND_out, A, B);
  sum sum_1 (.in_1(in_4), .in_2(B), .in_3(A), .out_4(Carry_Out), .out_5(sum_1_out_5));
  not not_1 (not_1_out, sum_1_out_5);
  not not_2 (not_2_out, in_4);
  and and_2 (and_2_out, not_1_out, not_2_out);
  or or_2 (or_2_out, OR_out, and_2_out);
  Multiplexer #(.select(3), .enable("false")) multiplexer_1 (
    .in0(OR_out), .in1(AND_out), .in2(sum_1_out_5), .in3(sum_1_out_5), .in4(or_2_out), .out(S), .sel(in_1));  // open: in5, in6, in7

  // Notes on the sheet:
  //   in_4: pull=up
  //   00 AND
  //   01 OR
  //   10 ADICIÓN
endmodule
