// Logisim project practica03.circ as structural Verilog
module Suma (
  input  in_1,
  input  in_2,
  input  in_3,
  output out_4,
  output out_5
);

  wire and_1_out, and_2_out, and_3_out, and_4_out, not_1_out, not_2_out, not_3_out;

  CarryOut carryout_1 (.in_1(in_3), .in_2(in_2), .in_3(in_1), .out_4(out_5));
  not not_1 (not_1_out, in_1);
  not not_2 (not_2_out, in_2);
  not not_3 (not_3_out, in_3);
  and and_1 (and_1_out, in_3, in_2, in_1);
  and and_2 (and_2_out, in_3, not_2_out, not_1_out);
  and and_3 (and_3_out, not_3_out, in_2, not_1_out);
  and and_4 (and_4_out, not_3_out, not_2_out, in_1);
  or or_1 (out_4, and_4_out, and_3_out, and_2_out, and_1_out);
endmodule

module CarryOut (
  input  in_1,
  input  in_2,
  input  in_3,
  output out_4
);

  wire and_1_out, and_2_out, and_3_out;

  and and_1 (and_1_out, in_1, in_3);
  and and_2 (and_2_out, in_1, in_2);
  or or_1 (out_4, and_1_out, and_2_out, and_3_out);
  and and_3 (and_3_out, in_2, in_3);
endmodule

module Alu_1_bit (
  input  in_1,
  input  A,
  input  B,
  input  [2:0] in_4,
  input  Carry_In,
  output Salida_1_bit,
  output Carry_Out
);

  wire and_2_out, and_3_out, and_4_out, And_out, multiplexer_1_out, not_1_out, not_2_out, not_3_out,
       not_4_out, or_2_out, Or_out, Suma_2_out_4, Suma_2_out_5, Suma_out_4, Suma_out_5;

  not not_1 (not_1_out, B);
  Multiplexer #(.enable("false")) multiplexer_1 (.in0(B), .in1(not_1_out), .out(multiplexer_1_out), .sel(in_1));
  not not_2 (not_2_out, A);
  not not_3 (not_3_out, B);
  and And (And_out, A, B);
  or Or (Or_out, A, B);
  Suma Suma (.in_1(A), .in_2(B), .in_3(Carry_In), .out_5(Suma_out_5), .out_4(Suma_out_4));
  and and_2 (and_2_out, not_2_out, not_3_out);
  Suma Suma_2 (.in_1(A), .in_2(multiplexer_1_out), .in_3(Carry_In), .out_5(Suma_2_out_5), .out_4(Suma_2_out_4));
  not not_4 (not_4_out, Or_out);
  and and_3 (and_3_out, And_out, Carry_In);
  or or_2 (or_2_out, and_3_out, and_4_out);
  and and_4 (and_4_out, Carry_In, and_2_out);
  Multiplexer #(.select(3), .enable("false")) multiplexer_2 (
    .in0(Carry_In), .in1(Carry_In), .in2(Suma_out_5), .in3(Suma_2_out_5), .in4(or_2_out), .in5(Carry_In),
    .in6(Carry_In), .in7(Carry_In), .out(Carry_Out), .sel(in_4));
  Multiplexer #(.select(3), .enable("false")) multiplexer_3 (
    .in0(And_out), .in1(Or_out), .in2(Suma_out_4), .in3(Suma_2_out_4), .in4(or_2_out), .in5(not_4_out),
    .out(Salida_1_bit), .sel(in_4));  // open: in6, in7
endmodule

module Alu_8_bits_suma (
  input  in_1,
  input  in_2,
  input  in_3,
  input  in_4,
  input  in_5,
  input  in_6,
  input  in_7,
  input  in_8,
  input  [2:0] Selector,
  input  in_10,
  input  in_11,
  input  in_12,
  input  in_13,
  input  in_14,
  input  in_15,
  input  in_16,
  input  in_17,
  output Salida,
  output Carry_Out,
  output out_20,
  output out_21,
  output out_22,
  output out_23,
  output out_24,
  output out_25,
  output out_26,
  output out_27
);

  wire alu_1_bit_1_carry_out, alu_1_bit_2_carry_out, alu_1_bit_3_carry_out, alu_1_bit_4_carry_out,
       alu_1_bit_5_carry_out, alu_1_bit_6_carry_out, alu_1_bit_7_carry_out, alu_1_bit_8_carry_out, and_1_out,
       and_2_out, and_3_out, and_4_out, multiplexer_1_out, not_1_out, not_2_out, not_3_out, not_4_out,
       not_5_out, or_1_out, or_2_out;

  Alu_1_bit alu_1_bit_1 (
    .A(in_8), .B(in_17), .Carry_In(or_1_out), .in_1(or_1_out), .in_4(Selector),
    .Carry_Out(alu_1_bit_1_carry_out), .Salida_1_bit(out_27));
  Alu_1_bit alu_1_bit_2 (
    .A(in_7), .B(in_16), .Carry_In(alu_1_bit_1_carry_out), .in_1(or_1_out), .in_4(Selector),
    .Carry_Out(alu_1_bit_2_carry_out), .Salida_1_bit(out_26));
  Alu_1_bit alu_1_bit_3 (
    .A(in_6), .B(in_15), .Carry_In(alu_1_bit_2_carry_out), .in_1(or_1_out), .in_4(Selector),
    .Carry_Out(alu_1_bit_3_carry_out), .Salida_1_bit(out_25));
  Multiplexer #(.enable("false")) multiplexer_1 (
    .in0(or_1_out), .in1(not_1_out), .out(multiplexer_1_out), .sel(and_1_out));
  not not_1 (not_1_out, or_1_out);
  Alu_1_bit alu_1_bit_4 (
    .A(in_5), .B(in_14), .Carry_In(alu_1_bit_3_carry_out), .in_1(or_1_out), .in_4(Selector),
    .Carry_Out(alu_1_bit_4_carry_out), .Salida_1_bit(out_24));
  Alu_1_bit alu_1_bit_5 (
    .A(in_4), .B(in_13), .Carry_In(alu_1_bit_4_carry_out), .in_1(or_1_out), .in_4(Selector),
    .Carry_Out(alu_1_bit_5_carry_out), .Salida_1_bit(out_23));
  Alu_1_bit alu_1_bit_6 (
    .A(in_3), .B(in_12), .Carry_In(alu_1_bit_5_carry_out), .in_1(or_1_out), .in_4(Selector),
    .Carry_Out(alu_1_bit_6_carry_out), .Salida_1_bit(out_22));
  Alu_1_bit alu_1_bit_7 (
    .A(in_2), .B(in_11), .Carry_In(alu_1_bit_6_carry_out), .in_1(or_1_out), .in_4(Selector),
    .Carry_Out(alu_1_bit_7_carry_out), .Salida_1_bit(out_21));
  not not_2 (not_2_out, alu_1_bit_8_carry_out);
  Alu_1_bit alu_1_bit_8 (
    .A(in_1), .B(in_10), .Carry_In(alu_1_bit_7_carry_out), .in_1(or_1_out), .in_4(Selector),
    .Carry_Out(alu_1_bit_8_carry_out), .Salida_1_bit(out_20));
  Multiplexer #(.enable("false")) multiplexer_2 (
    .in0(alu_1_bit_8_carry_out), .in1(not_2_out), .out(Carry_Out), .sel(multiplexer_1_out));
  or or_1 (or_1_out, and_1_out, and_2_out);
  not not_3 (not_3_out, Selector[0]);
  not not_4 (not_4_out, Selector[1]);
  and and_1 (and_1_out, not_3_out, Selector[2]);
  and and_2 (and_2_out, Selector[0], Selector[1], not_5_out);
  not not_5 (not_5_out, Selector[2]);
  and and_3 (and_3_out, out_27, out_26, out_25, out_24, out_23, out_22, out_21, out_20);
  or or_2 (or_2_out, out_27, out_26, out_25, out_24, out_23, out_22, out_21, out_20);
  and and_4 (and_4_out, out_27, out_26, out_25, out_24, out_23, out_22, out_21, out_20);
  Multiplexer #(.select(3), .enable("false")) multiplexer_3 (
    .in0(and_3_out), .in1(or_2_out), .in2(out_27), .in3(out_27), .in4(Carry_Out), .in5(and_4_out),
    .out(Salida), .sel(Selector));  // open: in6, in7
endmodule

module Alu_8_bits (
  input  [7:0] in_1,
  input  [2:0] in_2,
  input  [7:0] in_3,
  output out_4,
  output out_5,
  output [7:0] out_6
);

  Alu_8_bits_suma alu_8_bits_suma_1 (
    .in_1(in_1[7]), .in_2(in_1[6]), .in_3(in_1[5]), .in_4(in_1[4]), .in_5(in_1[3]), .in_6(in_1[2]),
    .in_7(in_1[1]), .in_8(in_1[0]), .Selector(in_2), .in_10(in_3[7]), .in_11(in_3[6]), .in_12(in_3[5]),
    .in_13(in_3[4]), .in_14(in_3[3]), .in_15(in_3[2]), .in_16(in_3[1]), .in_17(in_3[0]), .Carry_Out(out_5),
    .out_20(out_6[7]), .out_21(out_6[6]), .out_22(out_6[5]), .out_23(out_6[4]), .out_24(out_6[3]),
    .out_25(out_6[2]), .out_26(out_6[1]), .out_27(out_6[0]), .Salida(out_4));
endmodule

module _1a_fila (
  input  A,
  input  B,
  input  C,
  input  D,
  output out_5,
  output out_6,
  output out_7,
  output out_8,
  output out_9
);

  wire and_1_out, and_2_out, and_3_out, and_4_out, and_5_out, and_6_out, and_7_out, and_8_out, and_9_out,
       and_10_out, and_11_out, nA_out, nB_out, nC_out, nD_out;

  not nA (nA_out, A);
  not nB (nB_out, B);
  not nD (nD_out, D);
  not nC (nC_out, C);
  and and_1 (and_1_out, nA_out, nB_out, C);
  and and_2 (and_2_out, nA_out, C, nD_out);
  and and_3 (and_3_out, nB_out, nC_out, nD_out);
  and and_4 (and_4_out, nA_out, B, nC_out, D);
  and and_5 (and_5_out, nA_out, nD_out);
  and and_6 (and_6_out, A, nB_out, nC_out);
  and and_7 (and_7_out, nA_out, B, nC_out);
  and and_8 (and_8_out, nA_out, nC_out);
  and and_9 (and_9_out, nB_out, nC_out);
  and and_10 (and_10_out, nA_out, B, nD_out);
  and and_11 (and_11_out, nA_out, C);
  or or_1 (out_5, and_1_out, and_2_out, and_3_out, and_4_out);
  or or_2 (out_6, and_2_out, and_3_out);
  or or_3 (out_7, and_5_out, and_6_out, and_7_out);
  or or_4 (out_8, and_8_out, and_9_out, and_10_out);
  or or_5 (out_9, out_7, and_11_out);
endmodule

module _2a_fila (
  input  A,
  input  B,
  input  C,
  input  D,
  output out_5,
  output out_6,
  output out_7,
  output out_8,
  output out_9
);

  wire and_1_out, and_2_out, and_3_out, and_4_out, and_6_out, and_7_out, and_8_out, and_9_out, and_10_out,
       and_11_out, and_12_out, nA_out, nB_out, nC_out, nD_out;

  not nA (nA_out, A);
  not nB (nB_out, B);
  not nD (nD_out, D);
  not nC (nC_out, C);
  and and_1 (and_1_out, nA_out, nB_out);
  and and_2 (and_2_out, nA_out, nC_out, D);
  and and_3 (and_3_out, nA_out, C, nD_out);
  and and_4 (and_4_out, nB_out, nC_out, nD_out);
  and and_5 (out_6, nA_out, nB_out, nC_out, D);
  and and_6 (and_6_out, nA_out, B, nC_out);
  and and_7 (and_7_out, A, nB_out, nC_out);
  and and_8 (and_8_out, nA_out, C);
  and and_9 (and_9_out, nA_out, D);
  and and_10 (and_10_out, nB_out, nC_out);
  and and_11 (and_11_out, nA_out, C);
  and and_12 (and_12_out, nA_out, D);
  or or_1 (out_7, and_6_out, and_7_out, and_8_out, and_9_out);
  or or_2 (out_9, and_10_out, and_11_out, and_12_out);
  or or_3 (out_5, and_1_out, and_2_out, and_3_out, and_4_out);

  assign out_8 = out_6;
endmodule

module Numeros (
  input  [3:0] in_1,
  output [4:0] out_2,
  output [4:0] out_3,
  output [4:0] out_4
);

  _3a_fila u_3a_fila_1 (
    .A(in_1[3]), .B(in_1[2]), .C(in_1[1]), .D(in_1[0]), .out_6(out_4[1]), .out_8(out_4[3]));  // open: out_5, out_7, out_9
  _2a_fila u_2a_fila_1 (
    .A(in_1[3]), .B(in_1[2]), .C(in_1[1]), .D(in_1[0]), .out_5(out_3[0]), .out_6(out_3[1]), .out_7(out_3[2]),
    .out_8(out_3[3]), .out_9(out_3[4]));
  _1a_fila u_1a_fila_1 (
    .A(in_1[3]), .B(in_1[2]), .C(in_1[1]), .D(in_1[0]), .out_5(out_2[0]), .out_6(out_2[1]), .out_7(out_2[2]),
    .out_8(out_2[3]), .out_9(out_2[4]));

  assign {out_4[4], out_4[2], out_4[0]} = {3{out_2[4]}};
endmodule

module _3a_fila (
  input  A,
  input  B,
  input  C,
  input  D,
  output out_5,
  output out_6,
  output out_7,
  output out_8,
  output out_9
);

  wire and_1_out, and_2_out, and_3_out, and_4_out, and_5_out, and_6_out, and_7_out, and_8_out, and_9_out,
       nA_out, nB_out, nC_out, nD_out;

  not nA (nA_out, A);
  not nB (nB_out, B);
  not nD (nD_out, D);
  not nC (nC_out, C);
  and and_1 (and_1_out, nA_out, nC_out, nD_out);
  and and_2 (and_2_out, A, nB_out, nC_out);
  and and_3 (and_3_out, nA_out, nB_out, C);
  and and_4 (and_4_out, nA_out, C, D);
  or or_1 (out_8, and_1_out, and_2_out, and_3_out, and_4_out);
  and and_5 (and_5_out, nA_out, B);
  and and_6 (and_6_out, nA_out, nC_out, nD_out);
  and and_7 (and_7_out, nA_out, B, nC_out);
  and and_8 (and_8_out, nA_out, C, D);
  and and_9 (and_9_out, A, nB_out, nC_out);
  or or_2 (out_6, and_5_out, and_6_out, and_7_out, and_8_out, and_9_out);
endmodule

module Contador2 (
  input  in_1,
  output out_2,
  output out_3,
  output out_4,
  output out_5,
  output out_6
);

  wire and_1_out, and_2_out, and_3_out, and_4_out, and_5_out, and_6_out, and_7_out, and_8_out, d_ff_1_qn,
       d_ff_2_qn, d_ff_3_qn, d_ff_4_qn, nand_1_out, not_1_out, not_2_out, not_3_out, not_4_out, not_5_out,
       not_6_out, not_7_out, not_8_out, or_1_out;

  or or_1 (or_1_out, nand_1_out, not_2_out);
  not not_1 (not_1_out, in_1);
  not not_2 (not_2_out, and_1_out);
  and and_1 (and_1_out, d_ff_1_qn, nand_1_out);
  D_Flip_Flop d_ff_1 (.clk(in_1), .D(and_1_out), .Q(out_6), .Qn(d_ff_1_qn), .en(1'b1));  // open: preset, reset
  not not_3 (not_3_out, out_6);
  and and_2 (and_2_out, or_1_out, d_ff_1_qn);
  D_Flip_Flop d_ff_2 (.clk(and_2_out), .D(and_3_out), .Q(out_5), .Qn(d_ff_2_qn), .en(1'b1));  // open: preset, reset
  and and_3 (and_3_out, d_ff_2_qn, nand_1_out);
  not not_4 (not_4_out, d_ff_2_qn);
  and and_4 (and_4_out, or_1_out, d_ff_2_qn);
  and and_5 (and_5_out, d_ff_3_qn, nand_1_out);
  and and_6 (and_6_out, or_1_out, d_ff_3_qn);
  D_Flip_Flop d_ff_3 (.clk(and_4_out), .D(and_5_out), .Q(out_4), .Qn(d_ff_3_qn), .en(1'b1));  // open: preset, reset
  D_Flip_Flop d_ff_4 (.clk(and_6_out), .D(and_7_out), .Q(out_3), .Qn(d_ff_4_qn), .en(1'b1));  // open: preset, reset
  and and_7 (and_7_out, d_ff_4_qn, nand_1_out);
  not not_5 (not_5_out, out_6);
  not not_6 (not_6_out, out_4);
  not not_7 (not_7_out, out_5);
  not not_8 (not_8_out, out_3);
  nand nand_1 (nand_1_out, not_3_out, not_4_out, d_ff_3_qn, out_3);
  and and_8 (and_8_out, not_5_out, not_6_out, not_7_out, not_8_out);
  and and_9 (out_2, not_1_out, and_8_out);
endmodule

module Contador1 (
  output out_1,
  output out_2,
  output out_3,
  output out_4
);

  wire and_1_out, and_2_out, and_3_out, and_4_out, and_5_out, and_6_out, and_7_out, clock_1_out, d_ff_1_qn,
       d_ff_2_qn, d_ff_3_qn, d_ff_4_qn, nand_1_out, not_1_out, not_2_out, not_3_out, or_1_out;

  Clock clock_1 (.out(clock_1_out));
  or or_1 (or_1_out, nand_1_out, not_1_out);
  not not_1 (not_1_out, and_1_out);
  and and_1 (and_1_out, d_ff_1_qn, nand_1_out);
  D_Flip_Flop d_ff_1 (.clk(clock_1_out), .D(and_1_out), .Q(out_4), .Qn(d_ff_1_qn), .en(1'b1));  // open: preset, reset
  not not_2 (not_2_out, out_4);
  and and_2 (and_2_out, or_1_out, d_ff_1_qn);
  D_Flip_Flop d_ff_2 (.clk(and_2_out), .D(and_3_out), .Q(out_3), .Qn(d_ff_2_qn), .en(1'b1));  // open: preset, reset
  and and_3 (and_3_out, d_ff_2_qn, nand_1_out);
  not not_3 (not_3_out, d_ff_2_qn);
  and and_4 (and_4_out, or_1_out, d_ff_2_qn);
  and and_5 (and_5_out, d_ff_3_qn, nand_1_out);
  and and_6 (and_6_out, or_1_out, d_ff_3_qn);
  D_Flip_Flop d_ff_3 (.clk(and_4_out), .D(and_5_out), .Q(out_2), .Qn(d_ff_3_qn), .en(1'b1));  // open: preset, reset
  D_Flip_Flop d_ff_4 (.clk(and_6_out), .D(and_7_out), .Q(out_1), .Qn(d_ff_4_qn), .en(1'b1));  // open: preset, reset
  and and_7 (and_7_out, d_ff_4_qn, nand_1_out);
  nand nand_1 (nand_1_out, not_2_out, not_3_out, d_ff_3_qn, out_1);
endmodule

module Ejercicio1 (
  output [3:0] out_1
);

  wire [4:0] numeros_1_out_2, numeros_1_out_3, numeros_1_out_4;

  Contador1 contador1_1 (.out_1(out_1[3]), .out_2(out_1[2]), .out_3(out_1[1]), .out_4(out_1[0]));
  Numeros numeros_1 (.in_1(out_1), .out_2(numeros_1_out_2), .out_3(numeros_1_out_3), .out_4(numeros_1_out_4));
  DotMatrix #(.matrixcols(3), .matrixrows(5)) dotmatrix_1 (
    .col0(numeros_1_out_2), .col1(numeros_1_out_3), .col2(numeros_1_out_4));
endmodule

module EjercicioExtra (
);

  wire and_1_out, and_2_out, clock_1_out, not_1_out, not_2_out, not_3_out, not_4_out, not_5_out;
  wire [3:0] contador2_1_out_6, contador2_2_out_6, contador2_3_out_6;
  wire [4:0] numeros_1_out_2, numeros_1_out_3, numeros_1_out_4, numeros_2_out_2, numeros_2_out_3,
       numeros_2_out_4, numeros_3_out_2, numeros_3_out_3, numeros_3_out_4;

  DotMatrix #(.matrixcols(3), .matrixrows(5)) dotmatrix_1 (
    .col0(numeros_1_out_2), .col1(numeros_1_out_3), .col2(numeros_1_out_4));
  Numeros numeros_1 (
    .in_1(contador2_1_out_6), .out_2(numeros_1_out_2), .out_3(numeros_1_out_3), .out_4(numeros_1_out_4));
  not not_1 (not_1_out, contador2_2_out_6[2]);
  not not_2 (not_2_out, contador2_2_out_6[1]);
  and and_1 (and_1_out, contador2_2_out_6[3], not_1_out, not_2_out, contador2_2_out_6[0], clock_1_out);
  Contador2 contador2_1 (
    .in_1(and_1_out), .out_3(contador2_1_out_6[3]), .out_4(contador2_1_out_6[2]),
    .out_5(contador2_1_out_6[1]), .out_6(contador2_1_out_6[0]));  // open: out_2
  DotMatrix #(.matrixcols(3), .matrixrows(5)) dotmatrix_2 (
    .col0(numeros_2_out_2), .col1(numeros_2_out_3), .col2(numeros_2_out_4));
  Numeros numeros_2 (
    .in_1(contador2_2_out_6), .out_2(numeros_2_out_2), .out_3(numeros_2_out_3), .out_4(numeros_2_out_4));
  not not_3 (not_3_out, contador2_3_out_6[1]);
  not not_4 (not_4_out, contador2_3_out_6[2]);
  and and_2 (and_2_out, contador2_3_out_6[3], not_4_out, not_3_out, contador2_3_out_6[0], not_5_out);
  Contador2 contador2_2 (
    .in_1(and_2_out), .out_3(contador2_2_out_6[3]), .out_4(contador2_2_out_6[2]),
    .out_5(contador2_2_out_6[1]), .out_6(contador2_2_out_6[0]));  // open: out_2
  not not_5 (not_5_out, clock_1_out);
  DotMatrix #(.matrixcols(3), .matrixrows(5)) dotmatrix_3 (
    .col0(numeros_3_out_2), .col1(numeros_3_out_3), .col2(numeros_3_out_4));
  Numeros numeros_3 (
    .in_1(contador2_3_out_6), .out_2(numeros_3_out_2), .out_3(numeros_3_out_3), .out_4(numeros_3_out_4));
  Clock clock_1 (.out(clock_1_out));
  Contador2 contador2_3 (
    .in_1(clock_1_out), .out_3(contador2_3_out_6[3]), .out_4(contador2_3_out_6[2]),
    .out_5(contador2_3_out_6[1]), .out_6(contador2_3_out_6[0]));  // open: out_2
endmodule

module Ejercicio2 (
);

  wire clock_1_out;

  Clock #(.highDuration(2), .lowDuration(2)) clock_1 (.out(clock_1_out));
endmodule

module Ejercicio3 (
  input  ReadRegister,
  input  WriteRegister,
  input  [3:0] WriteData,
  output [3:0] DataA,
  output [3:0] DataB
);

  Registro registro_1 (
    .WriteRegister(WriteRegister), .in_3(WriteData[0]), .in_4(WriteData[1]), .in_5(WriteData[2]),
    .in_6(WriteData[3]), .ReadRegister(ReadRegister), .out_11(DataA[0]), .out_7(DataA[1]), .out_8(DataA[2]),
    .out_12(DataA[3]), .out_13(DataB[0]), .out_14(DataB[1]), .out_9(DataB[2]), .out_10(DataB[3]));
endmodule

module Registro (
  input  ReadRegister,
  input  WriteRegister,
  input  in_3,
  input  in_4,
  input  in_5,
  input  in_6,
  output out_7,
  output out_8,
  output out_9,
  output out_10,
  output out_11,
  output out_12,
  output out_13,
  output out_14
);

  wire and_1_out, and_2_out, d_ff_4_qn, not_1_out;

  and and_1 (and_1_out, WriteRegister, ReadRegister);
  not not_1 (not_1_out, ReadRegister);
  D_Flip_Flop d_ff_1 (.clk(and_1_out), .D(in_3), .Q(out_11), .en(WriteRegister));  // open: Qn, preset, reset
  D_Flip_Flop d_ff_2 (.clk(and_1_out), .D(in_4), .Q(out_7), .en(WriteRegister));  // open: Qn, preset, reset
  D_Flip_Flop d_ff_3 (.clk(and_1_out), .D(in_5), .Q(out_8), .en(WriteRegister));  // open: Qn, preset, reset
  D_Flip_Flop d_ff_4 (
    .clk(and_1_out), .D(in_6), .Q(out_12), .Qn(d_ff_4_qn), .en(WriteRegister));  // open: preset, reset
  D_Flip_Flop d_ff_5 (.clk(and_2_out), .D(in_3), .Q(out_13));  // open: Qn, preset, en, reset
  and and_2 (and_2_out, not_1_out, WriteRegister);
  D_Flip_Flop d_ff_6 (.clk(and_2_out), .D(in_4), .Q(out_14));  // open: Qn, preset, en, reset
  D_Flip_Flop d_ff_7 (.clk(and_2_out), .D(in_5), .Q(out_9));  // open: Qn, preset, en, reset
  D_Flip_Flop d_ff_8 (.clk(and_2_out), .D(in_6), .Q(out_10));  // open: Qn, preset, en, reset
endmodule
